// Logisim project ALU_Group07.circ as structural Verilog: 6 circuits, main circuit main
module main (
  output halt,
  output [8:0] counter,
  output [3:0] op,
  output [11:0] a,
  output [11:0] b,
  output [11:0] oracle,
  output [11:0] result,
  output err_oracle,
  output error,
  output ok,
  output start_delimiter
);

  wire and_1_out, and_2_out, clock_1_out, comparator_1_eq, comparator_2_eq;

  Clock clock_1 (.out(clock_1_out));
  Counter #(.width(9), .max('h1ff), .trigger("falling")) counter_1 (
    .Q(counter), .carry(halt), .clk(clock_1_out));  // open: load, D, count, clr
  RAM #(.addrWidth(12), .dataWidth(4), .bus("separate")) ram_1 (
    .addr({counter, 3'b000}), .data(op), .ld(1'b1));  // open: din, str, sel, clk, clr
  RAM #(.addrWidth(12), .dataWidth(12), .bus("separate")) ram_2 (
    .addr({counter, 3'b001}), .data(a), .ld(1'b1));  // open: din, str, sel, clk, clr
  RAM #(.addrWidth(12), .dataWidth(12), .bus("separate")) ram_3 (
    .addr({counter, 3'b010}), .data(b), .ld(1'b1));  // open: din, str, sel, clk, clr
  RAM #(.addrWidth(12), .dataWidth(12), .bus("separate")) ram_4 (
    .addr({counter, 3'b011}), .data(oracle), .ld(1'b1));  // open: din, str, sel, clk, clr
  RAM #(.addrWidth(12), .dataWidth(1), .bus("separate")) ram_5 (
    .addr({counter, 3'b100}), .data(err_oracle), .ld(1'b1));  // open: din, str, sel, clk, clr
  RAM #(.addrWidth(12), .dataWidth(1), .bus("separate")) ram_6 (
    .addr({counter, 3'b101}), .data(start_delimiter), .ld(1'b1));  // open: din, str, sel, clk, clr
  _12_bit_ALU u_12_bit_alu_1 (.ALU_code(op), .a(a), .b(b), .overflow(error), .result(result));
  Comparator #(.width(1), .mode("unsigned")) comparator_1 (
    .a(error), .b(err_oracle), .eq(comparator_1_eq));  // open: gt, lt
  Comparator #(.width(12)) comparator_2 (.a(result), .b(oracle), .eq(comparator_2_eq));  // open: gt, lt
  and and_1 (and_1_out, comparator_1_eq, error);
  and and_2 (and_2_out, comparator_2_eq, comparator_1_eq, ~error);  // AND_Gate
  or or_1 (ok, and_1_out, and_2_out);

  // Notes on the sheet:
  //   You must complete the circuit '12-bit ALU' instead.
  //   DO NOT EDIT THIS CIRCUIT!
endmodule

module _12_bit_ALU (
  input  [3:0] ALU_code,
  input  [11:0] a,
  input  [11:0] b,
  output [11:0] result,
  output overflow
);

  wire Add_overflow, Greater_than_out_3, Less_than_out_3, Subtract_out_4;
  wire [11:0] Add_out_4, and_1_out, Generate_0_out_1, Greater_than_out_4, Less_than_out_4, or_1_out,
       Subtract_out_3;

  _12bit_CLA Add (.in_1(b), .in_2(a), .in_3(1'b0), .out_4(Add_out_4), .Overflow(Add_overflow));
  generate_0 Generate_0 (.out_1(Generate_0_out_1));
  assign or_1_out = a | b;  // OR_Gate or_1, 12 bits wide
  assign and_1_out = b & a;  // AND_Gate and_1, 12 bits wide
  _12_bit_numeric_subtraction Subtract (.in_1(a), .in_2(b), .out_3(Subtract_out_3), .out_4(Subtract_out_4));
  less_than Less_than (.in_1(a), .in_2(b), .out_3(Less_than_out_3), .out_4(Less_than_out_4));
  greater_than Greater_than (.in_1(a), .in_2(b), .out_3(Greater_than_out_3), .out_4(Greater_than_out_4));
  Multiplexer #(.select(4), .width(12)) multiplexer_1 (
    .in0(Generate_0_out_1), .in1(or_1_out), .in2(and_1_out), .in3(Add_out_4), .in4(Subtract_out_3),
    .in5(Less_than_out_4), .in6(Greater_than_out_4), .out(result), .sel(ALU_code));  // open: in7, in8, in9, in10, in11, in12, in13, in14, in15, en
  Multiplexer #(.select(4)) multiplexer_2 (
    .in0(1'b0), .in1(1'b0), .in2(1'b0), .in3(Add_overflow), .in4(Subtract_out_4), .in5(Less_than_out_3),
    .in6(Greater_than_out_3), .out(overflow), .sel(ALU_code));  // open: in7, in8, in9, in10, in11, in12, in13, in14, in15, en

  // Notes on the sheet:
  //   This circuit is used as a block in the main circuit, and its layout must remain unchanged. The circuit called "main" should be the main circuit of this file.
  //   Do not change the circuit appearance.
  //   DO NOT CHANGE THE INPUTS AND OUTPUTS OF THIS CIRCUIT!
  //   Do not add/remove inputs or outputs. Do not even change their location or orientation.
  //   And
  //   Or
endmodule

module generate_0 (
  output [11:0] out_1
);

  assign out_1 = {{11{1'b0}}, 1'b0};  // Bit_Extender bit_extender_1
endmodule

module _12_bit_numeric_subtraction (
  input  [11:0] in_1,
  input  [11:0] in_2,
  output [11:0] out_3,
  output out_4
);

  wire [11:0] not_1_out;

  assign not_1_out = ~in_2;  // NOT_Gate not_1, 12 bits wide
  _12bit_CLA u_12bit_cla_1 (.in_1(in_1), .in_2(not_1_out), .in_3(1'b1), .out_4(out_3), .Overflow(out_4));
endmodule

module less_than (
  input  [11:0] in_1,
  input  [11:0] in_2,
  output out_3,
  output [11:0] out_4
);

  wire [11:0] n12bit_cla_1_out_4, not_1_out;

  assign not_1_out = ~in_2;  // NOT_Gate not_1, 12 bits wide
  _12bit_CLA u_12bit_cla_1 (.in_1(in_1), .in_2(not_1_out), .in_3(1'b1), .out_4(n12bit_cla_1_out_4), .Overflow(out_3));
  assign out_4 = {{11{1'b0}}, n12bit_cla_1_out_4[11]};  // Bit_Extender bit_extender_1
endmodule

module greater_than (
  input  [11:0] in_1,
  input  [11:0] in_2,
  output out_3,
  output [11:0] out_4
);

  wire [11:0] n12bit_cla_1_out_4, not_1_out;

  assign not_1_out = ~in_1;  // NOT_Gate not_1, 12 bits wide
  _12bit_CLA u_12bit_cla_1 (.in_1(not_1_out), .in_2(in_2), .in_3(1'b1), .out_4(n12bit_cla_1_out_4), .Overflow(out_3));
  assign out_4 = {{11{1'b0}}, n12bit_cla_1_out_4[11]};  // Bit_Extender bit_extender_1
endmodule
