// Logisim project SD_Group07.circ as structural Verilog: 4 circuits, main circuit main
module main (
  output [11:0] pc,
  output [11:0] r0,
  output [11:0] r1,
  output [11:0] r2,
  output [11:0] r3,
  output [11:0] r4,
  output [11:0] r5,
  output [11:0] r6,
  output [11:0] r7,
  output halt
);

  wire and_1_out, clock_1_out, control_logic_1_alu_source, control_logic_1_memread, control_logic_1_memtoreg,
       control_logic_1_memwrite, control_logic_1_regwrite, not_1_out, reset_out;
  wire [2:0] control_logic_1_rt;
  wire [3:0] control_logic_1_alu;
  wire [11:0] bit_extender_1_out, multiplexer_1_out, multiplexer_2_out, n12_bit_alu_1_result, ram_2_data,
       register_file_1_s, register_file_1_t;
  wire [12:0] ram_1_data;

  Halt halt_1 (.instruction(ram_1_data), .clock(clock_1_out), .reset(reset_out), .halt(halt));
  Clock clock_1 (.out(clock_1_out));
  Button reset (.out(reset_out));
  and and_1 (and_1_out, ~halt, clock_1_out);  // AND_Gate
  program_counter program_counter_1 (
    .Branch_relative(1'b0), .Branch_absolute(1'b0), .C(and_1_out), .Reset(reset_out), .out_6(pc));  // open: Branch_value
  Control_Logic control_logic_1 (
    .in_1(ram_1_data), .RegWrite(control_logic_1_regwrite), .MemToReg(control_logic_1_memtoreg),
    .MemWrite(control_logic_1_memwrite), .MemRead(control_logic_1_memread), .ALU(control_logic_1_alu),
    .ALU_Source(control_logic_1_alu_source), .Rt(control_logic_1_rt));
  RAM #(.addrWidth(12), .dataWidth(13)) ram_1 (
    .addr(pc), .data(ram_1_data), .sel(1'b1), .clk(and_1_out), .ld(1'b1), .clr(reset_out));
  assign bit_extender_1_out = {{9{1'b0}}, ram_1_data[2:0]};  // Bit_Extender bit_extender_1
  register_file register_file_1 (
    .rs(ram_1_data[5:3]), .rt(control_logic_1_rt), .rd(ram_1_data[8:6]), .data(multiplexer_2_out),
    .write(control_logic_1_regwrite), .clock(and_1_out), .reset(reset_out), .S(register_file_1_s),
    .T(register_file_1_t), .out_8(r0), .out_9(r1), .out_10(r2), .out_11(r3), .out_12(r4), .out_13(r5),
    .out_14(r6), .out_15(r7));
  _12_bit_ALU u_12_bit_alu_1 (
    .ALU_code(control_logic_1_alu), .a(register_file_1_s), .b(multiplexer_1_out),
    .result(n12_bit_alu_1_result));  // open: overflow
  Multiplexer #(.width(12), .enable("false")) multiplexer_1 (
    .in0(register_file_1_t), .in1(bit_extender_1_out), .out(multiplexer_1_out),
    .sel(control_logic_1_alu_source));
  RAM #(.addrWidth(12), .dataWidth(12), .bus("separate")) ram_2 (
    .addr(n12_bit_alu_1_result), .din(register_file_1_t), .data(ram_2_data), .str(control_logic_1_memwrite),
    .sel(1'b1), .clk(and_1_out), .ld(control_logic_1_memread), .clr(reset_out));
  not not_1 (not_1_out, control_logic_1_memtoreg);
  Multiplexer #(.width(12), .enable("false")) multiplexer_2 (
    .in0(ram_2_data), .in1(n12_bit_alu_1_result), .out(multiplexer_2_out), .sel(not_1_out));

  // Notes on the sheet:
  //   current instruction
  //   clock signal
  //   reset button
  //   RegWrite
  //   DO NOT CHANGE THE INPUTS AND OUTPUTS OF THIS CIRCUIT! Do not add/remove inputs or outputs. Do not even change their location or orientation.
  //   MemToReg
  //   Memread
  //   Memwrite
endmodule

module Halt (
  input  [12:0] instruction,
  input  clock,
  input  reset,
  output halt
);

  wire and_1_out, comparator_1_eq, comparator_2_gt, counter_1_carry, or_1_out, or_2_out;
  wire [11:0] counter_1_q;

  Comparator #(.width(13), .mode("unsigned")) comparator_1 (
    .a(instruction), .b({13{1'b0}}), .eq(comparator_1_eq));  // open: gt, lt
  Counter #(.width(12), .max('hfff), .trigger("falling")) counter_1 (
    .Q(counter_1_q), .carry(counter_1_carry), .clk(clock), .clr(reset));  // open: load, D, count
  or or_1 (or_1_out, comparator_1_eq, counter_1_carry);
  Comparator #(.width(12), .mode("unsigned")) comparator_2 (
    .a(counter_1_q), .b({12{1'b0}}), .gt(comparator_2_gt));  // open: eq, lt
  or or_2 (or_2_out, halt, and_1_out);
  and and_1 (and_1_out, or_1_out, comparator_2_gt);
  Register #(.width(1)) register_1 (.D(or_2_out), .Q(halt), .clk(clock), .clr(reset));  // open: en

  // Notes on the sheet:
  //   halt becomes and stays asserted if the instruction is 0000 (not in the first clock cycle) or the end of the counter is reached (2^12)
endmodule

module program_counter (
  input  Branch_relative,
  input  Branch_absolute,
  input  [11:0] Branch_value,
  input  C,
  input  Reset,
  output [11:0] out_6
);

  wire and_1_out;
  wire [1:0] priority_encoder_1_out;
  wire [11:0] multiplexer_1_out, undriven, undriven_2;

  _12bit_CLA u_12bit_cla_1 (.in_1(Branch_value), .in_2(out_6), .in_3(1'b0));  // open: out_4, Overflow
  and and_1 (and_1_out, ~Branch_relative, ~Branch_absolute);  // AND_Gate
  Priority_Encoder #(.select(2)) priority_encoder_1 (
    .in0(Branch_relative), .in1(Branch_absolute), .in2(and_1_out), .out(priority_encoder_1_out));  // open: in3, gs, en_out, en_in
  Multiplexer #(.select(2), .width(12), .enable("false")) multiplexer_1 (
    .in0(undriven), .in1(Branch_value), .in2(undriven_2), .out(multiplexer_1_out),
    .sel(priority_encoder_1_out));  // open: in3
  _12bit_register u_12bit_register_1 (.Input(multiplexer_1_out), .Reset(Reset), .Write(1'b1), .Clock(C), .out_5(out_6));
  _12bit_CLA u_12bit_cla_2 (.in_1(out_6), .in_2(12'h1), .in_3(1'b0));  // open: out_4, Overflow
endmodule

module Control_Logic (
  input  [12:0] in_1,
  output RegWrite,
  output MemToReg,
  output MemWrite,
  output MemRead,
  output [3:0] ALU,
  output ALU_Source,
  output [2:0] Rt
);

  wire and_1_out, and_2_out, and_3_out, and_4_out, not_1_out, not_2_out, not_3_out, not_4_out, not_5_out,
       not_7_out, not_8_out, not_9_out, or_1_out;
  wire [3:0] bit_extender_1_out, multiplexer_1_out, multiplexer_2_out;

  assign bit_extender_1_out = {{1{1'b1}}, in_1[2:0]};  // Bit_Extender bit_extender_1
  and and_1 (and_1_out, ~in_1[2], ~in_1[1], ~in_1[0], and_2_out);  // AND_Gate
  Multiplexer #(.width(4), .enable("false")) multiplexer_1 (
    .in0(bit_extender_1_out), .in1(4'b0000), .out(multiplexer_1_out), .sel(and_1_out));
  not not_1 (not_1_out, in_1[9]);
  not not_2 (not_2_out, in_1[10]);
  not not_3 (not_3_out, in_1[11]);
  not not_4 (not_4_out, in_1[12]);
  and and_2 (and_2_out, not_1_out, not_2_out, not_3_out, not_4_out);
  and and_3 (and_3_out, ~and_1_out, and_2_out);  // AND_Gate
  and and_4 (and_4_out, ~and_2_out, ~MemRead, ~MemWrite);  // AND_Gate
  not not_5 (not_5_out, and_4_out);
  Multiplexer #(.width(4), .enable("false")) multiplexer_2 (
    .in0(in_1[12:9]), .in1(multiplexer_1_out), .out(multiplexer_2_out), .sel(not_5_out));
  and and_5 (MemRead, in_1[9], not_2_out, not_3_out, in_1[12]);
  and and_6 (MemWrite, not_1_out, in_1[10], not_3_out, in_1[12]);
  not not_6 (RegWrite, MemWrite);
  not not_7 (not_7_out, MemRead);
  not not_8 (not_8_out, and_4_out);
  not not_9 (not_9_out, and_3_out);
  or or_1 (or_1_out, MemRead, MemWrite);
  Multiplexer #(.width(4), .enable("false")) multiplexer_3 (
    .in0(multiplexer_2_out), .in1(4'b0011), .out(ALU), .sel(or_1_out));
  Multiplexer #(.width(3), .enable("false")) multiplexer_4 (.in0(in_1[2:0]), .in1(in_1[8:6]), .out(Rt), .sel(MemWrite));
  or or_2 (ALU_Source, MemWrite, MemRead);

  assign MemToReg = MemRead;

  // Notes on the sheet:
  //   Unary
  //   Binary
  //   Lw
  //   Sw
endmodule
