// Logisim project memory.circ as structural Verilog
module _12bit_register (
  input  [11:0] Input,
  input  Reset,
  input  Write,
  input  Clock,
  output [11:0] out_5
);

  wire or_1_out;
  wire [11:0] multiplexer_1_out;

  Multiplexer #(.width(12), .enable("false")) multiplexer_1 (
    .in0(Input), .in1({12{1'b0}}), .out(multiplexer_1_out), .sel(Reset));
  or or_1 (or_1_out, Reset, Write);
  D_Flip_Flop #(.trigger("falling")) d_ff_1 (
    .clk(Clock), .D(multiplexer_1_out[5]), .Q(out_5[5]), .en(or_1_out));  // open: Qn, preset, reset
  D_Flip_Flop #(.trigger("falling")) d_ff_2 (
    .clk(Clock), .D(multiplexer_1_out[11]), .Q(out_5[11]), .en(or_1_out));  // open: Qn, preset, reset
  D_Flip_Flop #(.trigger("falling")) d_ff_3 (
    .clk(Clock), .D(multiplexer_1_out[4]), .Q(out_5[4]), .en(or_1_out));  // open: Qn, preset, reset
  D_Flip_Flop #(.trigger("falling")) d_ff_4 (
    .clk(Clock), .D(multiplexer_1_out[10]), .Q(out_5[10]), .en(or_1_out));  // open: Qn, preset, reset
  D_Flip_Flop #(.trigger("falling")) d_ff_5 (
    .clk(Clock), .D(multiplexer_1_out[3]), .Q(out_5[3]), .en(or_1_out));  // open: Qn, preset, reset
  D_Flip_Flop #(.trigger("falling")) d_ff_6 (
    .clk(Clock), .D(multiplexer_1_out[9]), .Q(out_5[9]), .en(or_1_out));  // open: Qn, preset, reset
  D_Flip_Flop #(.trigger("falling")) d_ff_7 (
    .clk(Clock), .D(multiplexer_1_out[2]), .Q(out_5[2]), .en(or_1_out));  // open: Qn, preset, reset
  D_Flip_Flop #(.trigger("falling")) d_ff_8 (
    .clk(Clock), .D(multiplexer_1_out[8]), .Q(out_5[8]), .en(or_1_out));  // open: Qn, preset, reset
  D_Flip_Flop #(.trigger("falling")) d_ff_9 (
    .clk(Clock), .D(multiplexer_1_out[1]), .Q(out_5[1]), .en(or_1_out));  // open: Qn, preset, reset
  D_Flip_Flop #(.trigger("falling")) d_ff_10 (
    .clk(Clock), .D(multiplexer_1_out[7]), .Q(out_5[7]), .en(or_1_out));  // open: Qn, preset, reset
  D_Flip_Flop #(.trigger("falling")) d_ff_11 (
    .clk(Clock), .D(multiplexer_1_out[0]), .Q(out_5[0]), .en(or_1_out));  // open: Qn, preset, reset
  D_Flip_Flop #(.trigger("falling")) d_ff_12 (
    .clk(Clock), .D(multiplexer_1_out[6]), .Q(out_5[6]), .en(or_1_out));  // open: Qn, preset, reset
endmodule
